// Logisim project lab_2.circ as structural Verilog
module seg7_dec (
  input  i_m3,
  input  i_m2,
  input  i_m1,
  input  i_m0,
  output o_seg0,
  output o_seg1,
  output o_seg2,
  output o_seg3,
  output o_seg4,
  output o_seg5,
  output o_seg6,
  output o_seg7
);

  wire and_1_out, and_2_out, and_3_out, and_4_out, and_6_out, and_7_out, and_8_out, and_9_out, and_10_out,
       and_11_out, and_12_out, and_13_out, and_14_out, not_1_out, not_2_out, not_3_out, not_4_out;

  not not_1 (not_1_out, i_m3);
  not not_2 (not_2_out, i_m2);
  not not_3 (not_3_out, i_m1);
  not not_4 (not_4_out, i_m0);
  and and_1 (and_1_out, not_1_out, not_2_out, not_3_out, i_m0);
  and and_2 (and_2_out, i_m2, not_3_out, not_4_out);
  and and_3 (and_3_out, i_m2, not_3_out, i_m0);
  and and_4 (and_4_out, i_m2, i_m1, not_4_out);
  and and_5 (o_seg2, not_2_out, i_m1, not_4_out);
  and and_6 (and_6_out, not_1_out, not_2_out, not_3_out, i_m0);
  and and_7 (and_7_out, i_m2, not_3_out, not_4_out);
  and and_8 (and_8_out, i_m2, i_m1, i_m0);
  and and_9 (and_9_out, i_m2, not_3_out);
  and and_10 (and_10_out, not_1_out, not_2_out, i_m0);
  and and_11 (and_11_out, not_2_out, i_m1);
  and and_12 (and_12_out, i_m1, i_m0);
  and and_13 (and_13_out, not_1_out, not_2_out, not_3_out);
  and and_14 (and_14_out, i_m2, i_m1, i_m0);
  or or_1 (o_seg0, and_1_out, and_2_out);
  or or_2 (o_seg1, and_3_out, and_4_out);
  or or_3 (o_seg3, and_6_out, and_7_out, and_8_out);
  or or_4 (o_seg4, i_m0, and_9_out);
  or or_5 (o_seg5, and_10_out, and_11_out, and_12_out);
  or or_6 (o_seg6, and_13_out, and_14_out);

  assign o_seg7 = 1'b1;
endmodule

module mux_2x1 (
  input  a,
  input  sel,
  input  b,
  output o
);

  wire and_1_out, and_2_out, not_1_out;

  not not_1 (not_1_out, sel);
  and and_1 (and_1_out, a, not_1_out);
  and and_2 (and_2_out, sel, b);
  or or_1 (o, and_1_out, and_2_out);
endmodule

module comp (
  input  v3,
  input  v2,
  input  v1,
  input  v0,
  output z
);

  wire and_1_out, and_2_out;

  and and_1 (and_1_out, v3, v2);
  and and_2 (and_2_out, v1, v3);
  or or_1 (z, and_1_out, and_2_out);
endmodule

module circuit_b (
  input  a,
  output o_a0,
  output o_a1,
  output o_a2,
  output o_a3,
  output o_a4,
  output o_a5,
  output o_a6
);


  assign o_a0 = a;
  assign o_a1 = 1'b0;
  assign o_a2 = 1'b0;
  assign o_a3 = a;
  assign o_a4 = a;
  assign o_a5 = a;
  assign o_a6 = 1'b1;
endmodule

module circuit_a (
  input  v2,
  input  v1,
  input  v0,
  output o2,
  output o1,
  output o0
);

  not not_1 (o1, v1);
  xor xor_1 (o2, v2, o1);

  assign o0 = v0;
endmodule

module part2 (
  input  v3,
  input  v2,
  input  v1,
  input  in_4,
  input  v0
);

  wire a0, a1, a2, a3, a4, a5, a6, a_0, a_1, a_2, a_3, a_4, a_5, a_6, circuit_a_1_o0, circuit_a_1_o1,
       circuit_a_1_o2, comp_1_z, mux_2x1_1_o, mux_2x1_2_o, mux_2x1_3_o, mux_2x1_4_o;

  comp comp_1 (.v3(v3), .v2(v2), .v1(v1), .v0(v0), .z(comp_1_z));
  circuit_a circuit_a_1 (.v2(v2), .v1(v1), .v0(v0), .o2(circuit_a_1_o2), .o1(circuit_a_1_o1), .o0(circuit_a_1_o0));
  circuit_b circuit_b_1 (.a(comp_1_z), .o_a0(a0), .o_a1(a1), .o_a2(a2), .o_a3(a3), .o_a4(a4), .o_a5(a5), .o_a6(a6));
  mux_2x1 mux_2x1_1 (.a(v3), .sel(comp_1_z), .b(in_4), .o(mux_2x1_1_o));
  mux_2x1 mux_2x1_2 (.a(v2), .sel(comp_1_z), .b(circuit_a_1_o2), .o(mux_2x1_2_o));
  mux_2x1 mux_2x1_3 (.a(v1), .sel(comp_1_z), .b(circuit_a_1_o1), .o(mux_2x1_3_o));
  mux_2x1 mux_2x1_4 (.a(v0), .sel(comp_1_z), .b(circuit_a_1_o0), .o(mux_2x1_4_o));
  seg7_dec seg7_dec_1 (
    .i_m3(mux_2x1_1_o), .i_m2(mux_2x1_2_o), .i_m1(mux_2x1_3_o), .i_m0(mux_2x1_4_o), .o_seg0(a_0),
    .o_seg1(a_1), .o_seg2(a_2), .o_seg3(a_3), .o_seg4(a_4), .o_seg5(a_5), .o_seg6(a_6));  // open: o_seg7
  _7_Segment_Display #(.active("false")) u_7_segment_display_1 (
    .g(a6), .f(a5), .a(a0), .b(a1), .e(a4), .d(a3), .c(a2));  // open: dp
  _7_Segment_Display #(.active("false")) u_7_segment_display_2 (
    .g(a_6), .f(a_5), .a(a_0), .b(a_1), .e(a_4), .d(a_3), .c(a_2));  // open: dp
endmodule

module part1 (
  input  i_m3,
  input  i_m2,
  input  i_m1,
  input  i_m0,
  output o_seg0,
  output o_seg1,
  output o_seg2,
  output o_seg3,
  output o_seg4,
  output o_seg5,
  output o_seg6,
  output o_seg7
);

  wire and_1_out, and_2_out, and_3_out, and_4_out, and_6_out, and_7_out, and_8_out, and_9_out, and_10_out,
       and_11_out, and_12_out, and_13_out, and_14_out, not_1_out, not_2_out, not_3_out, not_4_out;

  not not_1 (not_1_out, i_m3);
  not not_2 (not_2_out, i_m2);
  not not_3 (not_3_out, i_m1);
  not not_4 (not_4_out, i_m0);
  and and_1 (and_1_out, not_1_out, not_2_out, not_3_out, i_m0);
  and and_2 (and_2_out, i_m2, not_3_out, not_4_out);
  and and_3 (and_3_out, i_m2, not_3_out, i_m0);
  and and_4 (and_4_out, i_m2, i_m1, not_4_out);
  and and_5 (o_seg2, not_2_out, i_m1, not_4_out);
  and and_6 (and_6_out, not_1_out, not_2_out, not_3_out, i_m0);
  and and_7 (and_7_out, i_m2, not_3_out, not_4_out);
  and and_8 (and_8_out, i_m2, i_m1, i_m0);
  and and_9 (and_9_out, i_m2, not_3_out);
  and and_10 (and_10_out, not_1_out, not_2_out, i_m0);
  and and_11 (and_11_out, not_2_out, i_m1);
  and and_12 (and_12_out, i_m1, i_m0);
  and and_13 (and_13_out, not_1_out, not_2_out, not_3_out);
  and and_14 (and_14_out, i_m2, i_m1, i_m0);
  or or_1 (o_seg0, and_1_out, and_2_out);
  or or_2 (o_seg1, and_3_out, and_4_out);
  or or_3 (o_seg3, and_6_out, and_7_out, and_8_out);
  or or_4 (o_seg4, i_m0, and_9_out);
  or or_5 (o_seg5, and_10_out, and_11_out, and_12_out);
  or or_6 (o_seg6, and_13_out, and_14_out);
  _7_Segment_Display #(.active("false")) u_7_segment_display_1 (
    .g(o_seg6), .f(o_seg5), .a(o_seg0), .b(o_seg1), .e(o_seg4), .d(o_seg3), .c(o_seg2));  // open: dp

  assign o_seg7 = 1'b1;

  // Other names for the same wires on the sheet: a0 = o_seg0; a1 = o_seg1; a2 = o_seg2; a3 = o_seg3; a4 = o_seg4;
  //   a5 = o_seg5; a6 = o_seg6
endmodule

module full_adder (
  input  b,
  input  a,
  input  ci,
  output co,
  output s
);

  wire and_1_out, and_2_out, and_3_out, and_4_out, and_5_out, and_6_out, and_7_out, not_1_out, not_2_out,
       not_3_out;

  not not_1 (not_1_out, b);
  not not_2 (not_2_out, a);
  not not_3 (not_3_out, ci);
  and and_1 (and_1_out, a, b);
  and and_2 (and_2_out, ci, b);
  and and_3 (and_3_out, ci, a);
  and and_4 (and_4_out, not_3_out, not_2_out, b);
  and and_5 (and_5_out, not_3_out, a, not_1_out);
  and and_6 (and_6_out, ci, not_2_out, not_1_out);
  and and_7 (and_7_out, ci, a, b);
  or or_1 (co, and_1_out, and_2_out, and_3_out);
  or or_2 (s, and_4_out, and_5_out, and_6_out, and_7_out);
endmodule

module bit4_ripple_carry (
  input  i_b2,
  input  i_b1,
  input  i_b0,
  input  i_a2,
  input  i_a1,
  input  i_a0,
  input  i_cin,
  input  i_b3,
  input  i_a3,
  output o_s2,
  output o_s1,
  output o_s0,
  output o_cout,
  output o_s3
);

  wire and_1_out, and_2_out, and_3_out, and_4_out, and_5_out, and_6_out, and_7_out, and_8_out, and_9_out,
       and_10_out, and_11_out, and_12_out, and_13_out, and_14_out, and_15_out, and_16_out, and_17_out,
       and_18_out, and_19_out, and_20_out, and_21_out, and_22_out, and_23_out, and_24_out, and_25_out,
       and_26_out, and_27_out, and_28_out, not_1_out, not_2_out, not_3_out, not_4_out, not_5_out, not_6_out,
       not_7_out, not_8_out, not_9_out, not_10_out, not_11_out, not_12_out, or_1_out, or_5_out, or_7_out;

  not not_1 (not_1_out, i_b0);
  not not_2 (not_2_out, i_a0);
  not not_3 (not_3_out, i_cin);
  not not_4 (not_4_out, i_b3);
  not not_5 (not_5_out, i_a3);
  not not_6 (not_6_out, or_7_out);
  and and_1 (and_1_out, i_a0, i_b0);
  and and_2 (and_2_out, i_cin, i_b0);
  and and_3 (and_3_out, i_cin, i_a0);
  and and_4 (and_4_out, not_3_out, not_2_out, i_b0);
  and and_5 (and_5_out, not_3_out, i_a0, not_1_out);
  and and_6 (and_6_out, i_cin, not_2_out, not_1_out);
  and and_7 (and_7_out, i_cin, i_a0, i_b0);
  and and_8 (and_8_out, i_a3, i_b3);
  and and_9 (and_9_out, or_7_out, i_b3);
  and and_10 (and_10_out, or_7_out, i_a3);
  and and_11 (and_11_out, not_6_out, not_5_out, i_b3);
  and and_12 (and_12_out, not_6_out, i_a3, not_4_out);
  and and_13 (and_13_out, or_7_out, not_5_out, not_4_out);
  and and_14 (and_14_out, or_7_out, i_a3, i_b3);
  or or_1 (or_1_out, and_1_out, and_2_out, and_3_out);
  or or_2 (o_s0, and_4_out, and_5_out, and_6_out, and_7_out);
  or or_3 (o_cout, and_8_out, and_9_out, and_10_out);
  or or_4 (o_s3, and_11_out, and_12_out, and_13_out, and_14_out);
  not not_7 (not_7_out, i_b1);
  not not_8 (not_8_out, i_a1);
  not not_9 (not_9_out, or_1_out);
  and and_15 (and_15_out, i_a1, i_b1);
  and and_16 (and_16_out, or_1_out, i_b1);
  and and_17 (and_17_out, or_1_out, i_a1);
  and and_18 (and_18_out, not_9_out, not_8_out, i_b1);
  and and_19 (and_19_out, not_9_out, i_a1, not_7_out);
  and and_20 (and_20_out, or_1_out, not_8_out, not_7_out);
  and and_21 (and_21_out, or_1_out, i_a1, i_b1);
  or or_5 (or_5_out, and_15_out, and_16_out, and_17_out);
  or or_6 (o_s1, and_18_out, and_19_out, and_20_out, and_21_out);
  not not_10 (not_10_out, i_b2);
  not not_11 (not_11_out, i_a2);
  not not_12 (not_12_out, or_5_out);
  and and_22 (and_22_out, i_a2, i_b2);
  and and_23 (and_23_out, or_5_out, i_b2);
  and and_24 (and_24_out, or_5_out, i_a2);
  and and_25 (and_25_out, not_12_out, not_11_out, i_b2);
  and and_26 (and_26_out, not_12_out, i_a2, not_10_out);
  and and_27 (and_27_out, or_5_out, not_11_out, not_10_out);
  and and_28 (and_28_out, or_5_out, i_a2, i_b2);
  or or_7 (or_7_out, and_22_out, and_23_out, and_24_out);
  or or_8 (o_s2, and_25_out, and_26_out, and_27_out, and_28_out);
endmodule

module check_BCD (
  input  i_a3,
  input  i_a2,
  input  i_a1,
  input  i_a0,
  input  i_b3,
  input  i_b2,
  input  i_b1,
  input  i_b0,
  output o_error
);

  wire and_1_out, and_2_out, and_3_out, and_4_out, or_1_out, or_2_out;

  and and_1 (and_1_out, i_a3, i_a2);
  and and_2 (and_2_out, i_a1, i_a3);
  and and_3 (and_3_out, i_b3, i_b2);
  and and_4 (and_4_out, i_b1, i_b3);
  or or_1 (or_1_out, and_1_out, and_2_out);
  or or_2 (or_2_out, and_3_out, and_4_out);
  or or_3 (o_error, or_1_out, or_2_out);
endmodule

module bcd_add (
  input  i_a1,
  input  i_a0,
  input  i_b1,
  input  i_b0,
  output o_s2,
  output o_s1,
  output o_s0
);

  wire and_1_out, and_2_out, and_3_out, and_4_out, and_5_out, and_6_out, and_7_out, and_8_out, and_9_out,
       and_10_out, and_11_out, not_1_out, not_2_out, not_3_out, not_4_out;

  not not_1 (not_1_out, i_a1);
  not not_2 (not_2_out, i_a0);
  not not_3 (not_3_out, i_b1);
  not not_4 (not_4_out, i_b0);
  and and_1 (and_1_out, i_a0, i_b1, i_b0);
  and and_2 (and_2_out, i_a1, i_b1);
  and and_3 (and_3_out, i_a1, i_a0, i_b0);
  and and_4 (and_4_out, not_1_out, not_2_out, i_b1);
  and and_5 (and_5_out, not_1_out, i_a0, not_3_out, i_b0);
  and and_6 (and_6_out, not_1_out, i_b1, not_4_out);
  and and_7 (and_7_out, i_a1, not_2_out, not_3_out);
  and and_8 (and_8_out, i_a1, not_3_out, not_4_out);
  and and_9 (and_9_out, i_a1, i_a0, i_b1, i_b0);
  and and_10 (and_10_out, not_2_out, i_b0);
  and and_11 (and_11_out, i_a0, not_4_out);
  or or_1 (o_s2, and_1_out, and_2_out, and_3_out);
  or or_2 (o_s1, and_4_out, and_5_out, and_6_out, and_7_out, and_8_out, and_9_out);
  or or_3 (o_s0, and_10_out, and_11_out);
endmodule
